// Logisim project Ch7.circ as structural Verilog
module main (
);

  wire OpCode_out_9, RegA_out_9, RegB_out_9, RegC_out_9;
  wire [15:0] OpCode_output_2;

  Control_Logic Control_Logic ();
  HelperRegister OpCode (
    .out_9(OpCode_out_9), .Output_2(OpCode_output_2));  // open: Input_2, Output, Clock, Clock_3, out_10, out_12, out_11, Clock_4, Clock_2, Input
  HelperRegister RegB (
    .Clock_3(RegA_out_9), .out_9(RegB_out_9), .Output_2(OpCode_output_2));  // open: Input_2, Output, Clock, out_10, out_12, out_11, Clock_4, Clock_2, Input
  HelperRegister RegA (
    .Clock_3(OpCode_out_9), .out_9(RegA_out_9), .Output_2(OpCode_output_2));  // open: Input_2, Output, Clock, out_10, out_12, out_11, Clock_4, Clock_2, Input
  HelperRegister Param (
    .Clock_3(RegC_out_9), .Output_2(OpCode_output_2));  // open: Input_2, Output, Clock, out_10, out_12, out_9, out_11, Clock_4, Clock_2, Input
  HelperRegister RegC (
    .Clock_3(RegB_out_9), .out_9(RegC_out_9), .Output_2(OpCode_output_2));  // open: Input_2, Output, Clock, out_10, out_12, out_11, Clock_4, Clock_2, Input
  Instruction_Register Instruction_Register ();  // open: In, Out, Clock
  // _16_BIT_ALU 16_bit_alu_1: pin names not known
  // _16_bit_8_word_register Registers: pin names not known
  // _16_bit_8_word_register Memory: pin names not known
endmodule

// Helper
module HelperRegister (
  input  [15:0] Input,
  input  [15:0] Input_2,
  input  Clock,
  input  Clock_2,
  input  Clock_3,
  input  Clock_4,
  output [15:0] Output,
  output [15:0] Output_2,
  output out_9,
  output out_10,
  output out_11,
  output out_12
);

  D_Flip_Flop d_ff_1 (.clk(Clock), .D(Input[14]), .Q(Output[14]));  // open: Qn, preset, en, reset
  D_Flip_Flop d_ff_2 (.clk(Clock), .D(Input[6]), .Q(Output[6]));  // open: Qn, preset, en, reset
  D_Flip_Flop d_ff_3 (.clk(Clock), .D(Input[8]), .Q(Output[8]));  // open: Qn, preset, en, reset
  D_Flip_Flop d_ff_4 (.clk(Clock), .D(Input[10]), .Q(Output[10]));  // open: Qn, preset, en, reset
  D_Flip_Flop d_ff_5 (.clk(Clock), .D(Input[12]), .Q(Output[12]));  // open: Qn, preset, en, reset
  D_Flip_Flop d_ff_6 (.clk(Clock), .D(Input[13]), .Q(Output[13]));  // open: Qn, preset, en, reset
  D_Flip_Flop d_ff_7 (.clk(Clock), .D(Input[15]), .Q(Output[15]));  // open: Qn, preset, en, reset
  D_Flip_Flop d_ff_8 (.clk(Clock), .D(Input[0]), .Q(Output[0]));  // open: Qn, preset, en, reset
  D_Flip_Flop d_ff_9 (.clk(Clock), .D(Input[2]), .Q(Output[2]));  // open: Qn, preset, en, reset
  D_Flip_Flop d_ff_10 (.clk(Clock), .D(Input[4]), .Q(Output[4]));  // open: Qn, preset, en, reset
  D_Flip_Flop d_ff_11 (.clk(Clock), .D(Input[5]), .Q(Output[5]));  // open: Qn, preset, en, reset
  D_Flip_Flop d_ff_12 (.clk(Clock), .D(Input[7]), .Q(Output[7]));  // open: Qn, preset, en, reset
  D_Flip_Flop d_ff_13 (.clk(Clock), .D(Input[9]), .Q(Output[9]));  // open: Qn, preset, en, reset
  D_Flip_Flop d_ff_14 (.clk(Clock), .D(Input[11]), .Q(Output[11]));  // open: Qn, preset, en, reset
  D_Flip_Flop d_ff_15 (.clk(Clock), .D(Input[1]), .Q(Output[1]));  // open: Qn, preset, en, reset
  D_Flip_Flop d_ff_16 (.clk(Clock), .D(Input[3]), .Q(Output[3]));  // open: Qn, preset, en, reset

  assign Clock_2 = Clock;
  assign Clock_3 = Clock;
  assign Clock_4 = Clock;
  assign Input_2 = Input;
  assign out_9 = Clock;
  assign out_10 = Clock;
  assign out_11 = Clock;
  assign out_12 = Clock;
  assign Output_2 = Output;
endmodule

module Instruction_Register (
  input  [15:0] In,
  input  [15:0] Out,
  input  Clock
);
endmodule
